# Fritzing sketch skema rangkaian jemuran pakaian otomatis (saved by Fritzing 0.9.3b)
breadboards: 1

parts:
  Arduino_Nano = Arduino Nano (Rev3.0)
  YL-83_-_Control_Board = YL-83 Rain Sensor - Control Board
  YL-83_-_Detection_Board = YL-83 Rain Sensor - Detection Board
  MOTOR_DRIVER_ULN2003 = X113647 Stepper Driver Board [package=board]  # not connected
  MOTOR_STEPPER_28BYJ-48 = 28BYJ-48 Stepper Motor  # not connected
  LDR_sensor = LM393 LDR breakout [part_number=100027]  # not connected
  Push_Button = Round Pushbutton
  Lampu_LED = LEDs [package=led10mm]

nets:
  N1: Arduino_Nano.GND, Lampu_LED.C
  N2: Arduino_Nano.3V3, Push_Button.leg1
  N3: YL-83_-_Control_Board.POS, YL-83_-_Detection_Board.POS
  N4: YL-83_-_Control_Board.NEG, YL-83_-_Detection_Board.NEG
  N5: Push_Button.leg0, Lampu_LED.A

notes:
  IN1
  IN2
  IN3
  IN4

custom parts:
  YL-83 Rain Sensor - Control Board: The YL-83 is a rain sensor that has more resistance when dry and less resistance when wet. The module runs at 5V.
  YL-83 Rain Sensor - Detection Board: The YL-83 is a rain sensor that has more resistance when dry and less resistance when wet. The module runs at 5V.
  X113647 Stepper Driver Board: A common stepper motor driver board based on ULN2003APG darlington array
  28BYJ-48 Stepper Motor: 28BYJ-48 gear-reduction stepper motor (small)
